// Logisim project Logisim - Kopya.circ as structural Verilog: 1 circuit, main circuit main
module main (
);

  wire and_1_out, and_2_out, and_3_out, and_4_out, and_5_out, and_6_out, and_7_out, and_8_out, and_9_out,
       dipswitch_1_sw1, dipswitch_1_sw2, Elektrik_p1, Maste_Key_p1, Maste_Key_p2, Maste_Key_p3, Maste_Key_p4,
       not_1_out, not_2_out, not_3_out, not_4_out, not_5_out, not_6_out, not_7_out, not_8_out, not_9_out,
       not_10_out, not_11_out, not_12_out, not_14_out, not_15_out, or_1_out, or_2_out, or_3_out, or_4_out,
       Rezerve_p1, Rezerve_p2, Rezerve_p3, Rezerve_p4, Rezerve_p5;

  not not_1 (not_1_out, dipswitch_1_sw1);
  LED led_1 (.in(not_1_out));
  LED led_2 (.in(dipswitch_1_sw1));
  DipSwitch #(.number(2)) dipswitch_1 (.sw1(dipswitch_1_sw1), .sw2(dipswitch_1_sw2));
  LED led_3 (.in(and_8_out));
  not not_2 (not_2_out, and_1_out);
  LED led_4 (.in(not_2_out));
  LED led_5 (.in(and_1_out));
  and and_1 (and_1_out, not_3_out, dipswitch_1_sw2);
  not not_3 (not_3_out, dipswitch_1_sw1);
  LED led_6 (.in(and_6_out));
  LED led_7 (.in(and_4_out));
  LED led_8 (.in(and_2_out));
  LED led_9 (.in(and_9_out));
  LED led_10 (.in(and_7_out));
  LED led_11 (.in(and_5_out));
  LED led_12 (.in(and_3_out));
  LED led_13 (.in(not_15_out));
  LED led_14 (.in(not_14_out));
  LED led_15 (.in(Rezerve_p1));
  LED led_16 (.in(not_12_out));
  // DipSwitch #(.number(2)) Elektrik: pin names not known; wires that end beside it: Elektrik_p1
  // DipSwitch #(.number(4)) Maste_Key: pin names not known; wires that end beside it: Maste_Key_p1, Maste_Key_p2, Maste_Key_p3, Maste_Key_p4
  // DipSwitch #(.number(4)) Rezerve: pin names not known; wires that end beside it: Rezerve_p1, Rezerve_p2, Rezerve_p3, Rezerve_p4, Rezerve_p5
  or or_1 (or_1_out, Maste_Key_p1, Maste_Key_p1);
  not not_4 (not_4_out, Rezerve_p2);
  not not_5 (not_5_out, Maste_Key_p1);
  or or_2 (or_2_out, Maste_Key_p2, Maste_Key_p2);
  not not_6 (not_6_out, Rezerve_p3);
  not not_7 (not_7_out, Maste_Key_p2);
  or or_3 (or_3_out, Maste_Key_p3, Maste_Key_p3);
  not not_8 (not_8_out, Rezerve_p4);
  not not_9 (not_9_out, Maste_Key_p3);
  or or_4 (or_4_out, Maste_Key_p4, Maste_Key_p4);
  not not_10 (not_10_out, Rezerve_p5);
  not not_11 (not_11_out, Maste_Key_p4);
  not not_12 (not_12_out, not_4_out);
  not not_13 (Rezerve_p1, not_6_out);
  not not_14 (not_14_out, not_8_out);
  not not_15 (not_15_out, not_10_out);
  and and_2 (and_2_out, or_1_out, not_4_out);
  and and_3 (and_3_out, not_4_out, not_5_out);
  and and_4 (and_4_out, or_2_out, not_6_out);
  and and_5 (and_5_out, not_6_out, not_7_out);
  and and_6 (and_6_out, or_3_out, not_8_out);
  and and_7 (and_7_out, not_8_out, not_9_out);
  and and_8 (and_8_out, or_4_out, not_10_out);
  and and_9 (and_9_out, not_10_out, not_11_out);
  LED led_17 (.in(Elektrik_p1));
  LED led_18 (.in(and_2_out));
  LED led_19 (.in(not_12_out));
  LED led_20 (.in(and_3_out));
  LED led_21 (.in(and_4_out));
  LED led_22 (.in(Rezerve_p1));
  LED led_23 (.in(and_5_out));
  LED led_24 (.in(and_6_out));
  LED led_25 (.in(not_14_out));
  LED led_26 (.in(and_7_out));
  LED led_27 (.in(and_8_out));
  LED led_28 (.in(not_15_out));
  LED led_29 (.in(and_9_out));
endmodule
